# Fritzing sketch familiarization (saved by Fritzing 0.9.10b)
breadboards: 1

parts:
  U1 = 4071 4 x 2 Input OR Gate, single part [part_number=4071 package="DIP (Dual Inline) [THT]"]
  U2 = 4081 4 x 2 Input AND Gate, single part [part_number=4081 package="DIP (Dual Inline) [THT]"]
  U3 = 4081 4 x 2 Input AND Gate, single part [part_number=4081 package="DIP (Dual Inline) [THT]"]
  U4 = 74HC04_HEX_INVERTER [package=dil14]
  R1 = Resistor [tolerance=±5% resistance=220 package="2512 [SMD]"]
  LED1 = LED - 3mm [color="Red (633nm)" current=0.030 package="3 mm [THT]"]

nets:
  GND: U1.GND, U2.GND, U3.GND, U4.GND, LED1.cathode
  VDD: U1.VDD, U2.VDD, U3.VDD, U4.VCC
  N1: U2.B2, R1.Pin_0
  N2: R1.Pin_1, LED1.anode

notes:
  input A (shown true)
  input D (shown false)
  OR
  AND
  NOT
