# Fritzing sketch metrology (saved by Fritzing 0.9.10b)
breadboards: 1

parts:
  Part1 = Arduino-MKR1000
  R1 = Resistor [tolerance=±5% power=0.25 resistance=220 package=THT]
  R2 = Resistor [tolerance=±5% power=0.25 resistance=220 package=THT]

nets:
  N1: Part1.connector2, R1.Pin_1, R2.Pin_1
  N2: Part1.connector24, R2.Pin_0

notes:
  R2
  R1
